# Fritzing sketch shematic nano + HC-05 (saved by Fritzing 0.8.3b)

parts:
  Part1 = Bluetooth HC-05 Macho
  Part2 = Arduino Micro (Rev3)

nets:
  N1: Part1.TXD, Part2.D2/SDA
  N2: Part1.RXD, Part2.D3/SCL
